// Logisim project ALU.circ as structural Verilog: 1 circuit, main circuit main
module main (
  input  [7:0] in_1,
  input  [7:0] in_2,
  input  in_3,
  output [7:0] out_4
);

  wire [7:0] adder_1_out;

  Adder adder_1 (.a(in_1), .b(in_2), .out(adder_1_out));  // open: cin, cout
  Multiplexer #(.width(8)) multiplexer_1 (.in1(adder_1_out), .out(out_4), .sel(in_3));  // open: in0, en
endmodule
