// Logisim project Instruction_decoder.circ as structural Verilog: 4 circuits, main circuit main
module main (
  input  [7:0] in_1,
  output out_2,
  output out_3,
  output out_4,
  output out_5,
  output [7:0] out_6,
  output [7:0] out_7
);

  op_code_decoder op_code_decoder_1 (
    .in_1(in_1[7]), .in_2(in_1[6]), .out_5(out_4), .out_3(out_2), .out_6(out_5), .out_4(out_3));
  register_1_decoder register_1_decoder_1 (.in_1(in_1[5]), .in_2(in_1[4]), .in_3(in_1[3]), .out_4(out_6));
  register_2_decoder register_2_decoder_1 (.in_1(in_1[2]), .in_2(in_1[1]), .in_3(in_1[0]), .out_4(out_7));
endmodule

module op_code_decoder (
  input  in_1,
  input  in_2,
  output out_3,
  output out_4,
  output out_5,
  output out_6
);

  Decoder #(.select(2), .enable("false")) decoder_1 (
    .out0(out_5), .out1(out_3), .out2(out_6), .out3(out_4), .sel({in_1, in_2}));
endmodule

module register_1_decoder (
  input  in_1,
  input  in_2,
  input  in_3,
  output [7:0] out_4
);

  Decoder #(.select(3), .enable("false")) decoder_1 (
    .out0(out_4[7]), .out1(out_4[6]), .out2(out_4[5]), .out3(out_4[4]), .out4(out_4[3]), .out5(out_4[2]),
    .out6(out_4[1]), .out7(out_4[0]), .sel({in_1, in_2, in_3}));
endmodule

module register_2_decoder (
  input  in_1,
  input  in_2,
  input  in_3,
  output [7:0] out_4
);

  Decoder #(.select(3), .enable("false")) decoder_1 (
    .out0(out_4[7]), .out1(out_4[6]), .out2(out_4[5]), .out3(out_4[4]), .out4(out_4[3]), .out5(out_4[2]),
    .out6(out_4[1]), .out7(out_4[0]), .sel({in_1, in_2, in_3}));
endmodule
