// Logisim project PC.circ as structural Verilog: 1 circuit, main circuit main
module main (
  input  in_1,
  output [4:0] out_2
);

  Counter #(.width(5), .max('h17), .ongoal("stay")) counter_1 (
    .Q(out_2), .clk(in_1));  // open: load, D, count, carry, clr
endmodule
