// Logisim project Register_file.circ as structural Verilog: 4 circuits, main circuit main
module main (
  input  [7:0] in_1,
  input  [7:0] in_2,
  input  [7:0] RAM,
  input  [7:0] RAM_2,
  input  [7:0] ALU,
  output [7:0] out_6,
  output [7:0] out_7,
  output [7:0] out_8,
  output [7:0] out_9,
  output [7:0] out_10
);

  wire xor_1_out, xor_2_out;
  wire [7:0] register_a_1_out_2, register_b_1_out_2;

  xor xor_1 (xor_1_out, in_2[5], in_1[5]);
  xor xor_2 (xor_2_out, in_2[4], in_1[4]);
  register_A register_a_1 (.Enabler(in_1[7]), .out_2(register_a_1_out_2));
  register_B register_b_1 (.Enabler(in_1[6]), .out_2(register_b_1_out_2));
  Register register_1 (.D(RAM), .Q(out_7), .clk(xor_1_out));  // open: en, clr
  Register register_2 (.D(RAM_2), .Q(out_8), .clk(xor_2_out));  // open: en, clr
  register_C register_c_1 (.Enabler(in_2[3]), .out_2(out_9));
  Register register_3 (.D(ALU), .Q(out_10), .clk(in_1[2]));  // open: en, clr
  Multiplexer #(.width(8)) multiplexer_1 (
    .in0(register_a_1_out_2), .in1(register_b_1_out_2), .out(out_6), .sel(in_1[6]));  // open: en

  // Notes on the sheet:
  //   00 Holds memory address of Matrix A
  //   01 Holds memory address of Matrix B
  //   10 Holds value from memory A
  //   11 Holds value from memory B
  //   100 Holds memory address of Matrix C
  //   101 Holds value from ALU
endmodule

module register_A (
  input  Enabler,
  output [7:0] out_2
);

  wire [7:0] counter_1_q;

  Counter #(.ongoal("load")) counter_1 (.Q(counter_1_q), .clk(Enabler));  // open: load, D, count, carry, clr
  Adder adder_1 (.a(counter_1_q), .b({8{1'b0}}), .out(out_2));  // open: cin, cout
endmodule

module register_B (
  input  Enabler,
  output [7:0] out_2
);

  wire [7:0] counter_1_q;

  Counter #(.ongoal("load")) counter_1 (.Q(counter_1_q), .clk(Enabler));  // open: load, D, count, carry, clr
  Adder adder_1 (.a(counter_1_q), .b(8'h3), .out(out_2));  // open: cin, cout
endmodule

module register_C (
  input  Enabler,
  output [7:0] out_2
);

  wire and_1_out, counter_1_carry;
  wire [7:0] adder_1_out, adder_2_out, counter_1_q, counter_2_q;

  Counter #(.max('h5), .ongoal("stay")) counter_1 (
    .Q(counter_1_q), .carry(counter_1_carry), .clk(Enabler));  // open: load, D, count, clr
  Adder adder_1 (.a(counter_1_q), .b(8'h7), .out(adder_1_out));  // open: cin, cout
  and and_1 (and_1_out, counter_1_carry, Enabler);
  Multiplexer #(.width(8)) multiplexer_1 (
    .in0(adder_1_out), .in1(adder_2_out), .out(out_2), .sel(counter_1_carry));  // open: en
  Counter #(.max('h4), .ongoal("stay")) counter_2 (
    .Q(counter_2_q), .clk(and_1_out));  // open: load, D, count, carry, clr
  Adder adder_2 (.a(counter_2_q), .b(8'h7), .out(adder_2_out));  // open: cin, cout
endmodule
