// Logisim project lab6.circ as structural Verilog: 2 circuits, main circuit main
module main (
  input  in_1,
  input  in_2,
  output [7:0] out_3,
  output [7:0] out_4,
  output [7:0] out_5,
  output [7:0] out_6,
  output [7:0] out_7
);

  wire and_1_out, button_1_out, clock_1_out, clock_2_out, clock_3_out, CPU_out_8, CPU_out_9, CPU_out_10,
       Instruction_decoder_out_2, Instruction_decoder_out_3, Instruction_decoder_out_4,
       Instruction_decoder_out_5, t_ff_1_q, xor_1_out, xor_2_out, xor_3_out, xor_4_out, xor_5_out, xor_6_out;
  wire [4:0] CPU_out_4, PC_out_2;
  wire [7:0] ALU_out_4, CPU_out_5, CPU_out_6, CPU_outputs, Instruction_decoder_out_6,
       Instruction_decoder_out_7, multiplexer_1_out, multiplexer_2_out, ram_2_data, Register_file_out_7,
       Register_file_out_8, Register_file_out_10, rom_2_data;

  PC_main PC (.in_1(in_1), .out_2(PC_out_2));
  ROM #(.addrWidth(5)) rom_1 (.addr(PC_out_2), .data(out_4), .sel(in_2));
  Instruction_decoder_main Instruction_decoder (
    .in_1(out_4), .out_4(Instruction_decoder_out_4), .out_2(Instruction_decoder_out_2),
    .out_5(Instruction_decoder_out_5), .out_3(Instruction_decoder_out_3), .out_6(Instruction_decoder_out_6),
    .out_7(Instruction_decoder_out_7));
  ALU_main ALU (
    .in_1(Register_file_out_7), .in_2(Register_file_out_8), .in_3(Instruction_decoder_out_3),
    .out_4(ALU_out_4));
  CPU CPU (
    .out_4(CPU_out_4), .out_5(CPU_out_5), .out_6(CPU_out_6), .Outputs(CPU_outputs), .in_1(rom_2_data),
    .in_3(ram_2_data), .Input_Lines(and_1_out), .out_8(CPU_out_8), .out_9(CPU_out_9), .out_10(CPU_out_10));
  Register_file_main Register_file (
    .RAM(out_5), .RAM_2(out_5), .ALU(ALU_out_4), .in_1(Instruction_decoder_out_6),
    .in_2(Instruction_decoder_out_7), .out_6(out_6), .out_7(Register_file_out_7),
    .out_8(Register_file_out_8), .out_9(out_7), .out_10(Register_file_out_10));
  xor xor_1 (xor_1_out, xor_4_out, Instruction_decoder_out_4);
  ROM #(.addrWidth(5)) rom_2 (.addr(CPU_out_4), .data(rom_2_data), .sel(t_ff_1_q));
  Multiplexer #(.width(8)) multiplexer_1 (
    .in0(out_7), .in1(out_6), .out(multiplexer_1_out), .sel(xor_1_out));  // open: en
  ExactlyOne xor_2 (
    .out(xor_2_out), .in0(Instruction_decoder_out_5), .in1(Instruction_decoder_out_2),
    .in2(Instruction_decoder_out_4));
  Multiplexer #(.width(8)) multiplexer_2 (
    .in0(CPU_out_6), .in1(CPU_out_5), .out(multiplexer_2_out), .sel(xor_3_out));  // open: en
  xor xor_3 (xor_3_out, CPU_out_8, xor_5_out);
  Clock clock_1 (.out(clock_1_out));
  xor xor_4 (xor_4_out, Instruction_decoder_out_2, Instruction_decoder_out_4);
  Clock clock_2 (.out(clock_2_out));
  xor xor_5 (xor_5_out, CPU_out_9, CPU_out_8);
  ExactlyOne xor_6 (.out(xor_6_out), .in0(CPU_out_10), .in1(CPU_out_9), .in2(CPU_out_8));
  RAM #(.bus("separate")) ram_1 (
    .addr(multiplexer_1_out), .din(Register_file_out_10), .data(out_5), .str(Instruction_decoder_out_5),
    .sel(xor_2_out), .clk(clock_1_out), .ld(xor_4_out));  // open: clr
  RAM #(.bus("separate")) ram_2 (
    .addr(multiplexer_2_out), .din(CPU_outputs), .data(ram_2_data), .str(CPU_out_10), .sel(xor_6_out),
    .clk(clock_2_out), .ld(xor_5_out));  // open: clr
  Button button_1 (.out(button_1_out));
  Multiplexer #(.width(8)) multiplexer_3 (.in1(ram_2_data), .out(out_3), .sel(CPU_out_8));  // open: in0, en
  T_Flip_Flop t_ff_1 (
    .clk(button_1_out), .T(button_1_out), .Q(t_ff_1_q), .en(button_1_out));  // open: Qn, preset, reset
  Clock #(.highDuration(4)) clock_3 (.out(clock_3_out));
  and and_1 (and_1_out, t_ff_1_q, clock_3_out);

  // Notes on the sheet:
  //   contents of rom_1 (hex, n*v repeats v):
  //   42 4b d3 ac 42 4b d3 ac 42 4b d3 ac 42 4b d3 ac 0 3c 0 3c 0 3c 0 3c
  //   The design here is meant to demo the bare bones of the processor. The above design is the same design here, except it has been organized
  //   contents of rom_2 (hex, n*v repeats v):
  //   42 4b d3 ac 42 4b d3 ac 42 4b d3 ac 42 4b d3 ac 0 3c 0 3c 0 3c 0 3c
endmodule

module CPU (
  input  [7:0] in_1,
  input  Input_Lines,
  input  [7:0] in_3,
  output [4:0] out_4,
  output [7:0] out_5,
  output [7:0] out_6,
  output [7:0] Outputs,
  output out_8,
  output out_9,
  output out_10
);

  wire Add;
  wire [7:0] ALU_out_4, INSTRUCTION_DECODER_out_6, INSTRUCTION_DECODER_out_7, REGISTER_FILE_out_7,
       REGISTER_FILE_out_8;

  PC_main PC (.in_1(Input_Lines), .out_2(out_4));
  Instruction_decoder_main INSTRUCTION_DECODER (
    .in_1(in_1), .out_4(out_8), .out_2(out_9), .out_5(out_10), .out_3(Add),
    .out_6(INSTRUCTION_DECODER_out_6), .out_7(INSTRUCTION_DECODER_out_7));
  Register_file_main REGISTER_FILE (
    .RAM(in_3), .RAM_2(in_3), .ALU(ALU_out_4), .in_1(INSTRUCTION_DECODER_out_6),
    .in_2(INSTRUCTION_DECODER_out_7), .out_6(out_5), .out_7(REGISTER_FILE_out_7),
    .out_8(REGISTER_FILE_out_8), .out_9(out_6), .out_10(Outputs));
  ALU_main ALU (.in_1(REGISTER_FILE_out_7), .in_2(REGISTER_FILE_out_8), .in_3(Add), .out_4(ALU_out_4));

  // Other names for the same wires on the sheet: Load = out_9; Load_Mem_Add[7:0] = out_5; PC_Input = Input_Lines;
  //   RAM1[7:0] = in_3; Read = out_8; Register3[7:0] = Outputs; ROM[4:0] = out_4; ROM2[7:0] = in_1; Store = out_10;
  //   Store_Mem_Add[7:0] = out_6

  // Notes on the sheet:
  //   Output Lines
  //   Inputs
endmodule
