// Logisim project Lab2_prob1.circ as structural Verilog: 1 circuit, main circuit main
module main (
  input  a,
  input  b,
  input  c,
  input  a_2,
  input  b_2,
  input  c_2,
  output F,
  output G
);

  wire and_1_out, and_2_out, and_3_out, and_4_out, and_5_out, and_6_out, and_7_out, and_8_out, not_1_out,
       not_2_out, or_1_out, or_2_out, or_3_out, or_5_out, or_6_out;

  not not_1 (not_1_out, a_2);
  not not_2 (not_2_out, b_2);
  and and_1 (and_1_out, a, b);
  and and_2 (and_2_out, not_1_out, not_2_out);
  and and_3 (and_3_out, not_2_out, a_2);
  and and_4 (and_4_out, b_2, a_2);
  and and_5 (and_5_out, and_1_out, c);
  and and_6 (and_6_out, and_2_out, c_2);
  and and_7 (and_7_out, and_3_out, c_2);
  and and_8 (and_8_out, and_4_out, c_2);
  or or_1 (or_1_out, and_6_out, and_7_out);
  or or_2 (or_2_out, and_1_out, and_5_out);
  or or_3 (or_3_out, a, b);
  or or_4 (G, or_1_out, and_8_out);
  or or_5 (or_5_out, or_2_out, or_3_out);
  or or_6 (or_6_out, or_3_out, c);
  or or_7 (F, or_5_out, or_6_out);

  // Notes on the sheet:
  //   ab
  //   a'b'
  //   ab'
  //   ab
  //   abc
  //   a'b'c
  //   ab'c
  //   abc
  //   a'b'c + ab'c
  //   ab + abc
  //   a + b
  //   (a'b'c + ab'c) + abc
  //   (ab + abc) + (a + b)
  //   (a + b) + c
  //   ((ab + abc) + (a + b)) + ((a + b) + c)
endmodule
