// Logisim project lab2_prob2.circ as structural Verilog: 1 circuit, main circuit main
module main (
  input  Car_0,
  input  Car_1,
  input  Car_2,
  input  Car_3,
  input  Car_4,
  input  Car_5,
  input  Car_6
);

  wire and_1_out, and_2_out, and_3_out, and_4_out, and_5_out, and_6_out, and_7_out, and_8_out, and_9_out,
       and_10_out, and_11_out, and_12_out, not_1_out, not_2_out, not_3_out, not_4_out, not_5_out, not_6_out,
       not_7_out, not_8_out, not_9_out, not_10_out, not_11_out, not_12_out, not_13_out, or_1_out, or_2_out,
       or_3_out, or_4_out, or_5_out, or_6_out, or_7_out, or_8_out, or_9_out, or_10_out, or_11_out, or_12_out,
       or_13_out, or_14_out, xnor_1_out, xnor_2_out;

  _7_Segment_Display u_7_segment_display_1 (
    .g(or_14_out), .f(or_13_out), .a(or_9_out), .b(or_10_out), .e(and_12_out), .d(or_12_out), .c(or_11_out));  // open: dp
  and and_1 (and_1_out, Car_0, Car_1, Car_2, Car_3, Car_4, Car_5, Car_6);
  or or_1 (or_1_out, Car_4, Car_5, Car_6);
  or or_2 (or_2_out, Car_2, Car_3, Car_6);
  or or_3 (or_3_out, Car_1, Car_3, Car_5);
  and and_2 (and_2_out, or_2_out, not_1_out);
  not not_1 (not_1_out, or_3_out);
  not not_2 (not_2_out, and_1_out);
  not not_3 (not_3_out, or_1_out);
  not not_4 (not_4_out, or_3_out);
  and and_3 (and_3_out, not_2_out, not_3_out);
  not not_5 (not_5_out, and_1_out);
  not not_6 (not_6_out, or_3_out);
  not not_7 (not_7_out, or_2_out);
  not not_8 (not_8_out, or_2_out);
  or or_4 (or_4_out, not_4_out, and_3_out);
  and and_4 (and_4_out, not_11_out, not_5_out);
  or or_5 (or_5_out, and_4_out, not_6_out);
  or or_6 (or_6_out, not_7_out, and_2_out);
  not not_9 (not_9_out, or_2_out);
  not not_10 (not_10_out, or_3_out);
  or or_7 (or_7_out, or_1_out, or_3_out);
  and and_5 (and_5_out, or_1_out, not_8_out);
  and and_6 (and_6_out, or_2_out, or_4_out);
  and and_7 (and_7_out, and_1_out, or_3_out);
  xnor xnor_1 (xnor_1_out, or_1_out, or_3_out);
  xnor xnor_2 (xnor_2_out, or_3_out, or_2_out);
  not not_11 (not_11_out, or_1_out);
  buf and_8 (and_8_out, or_7_out);  // AND_Gate
  and and_9 (and_9_out, or_2_out, or_5_out);
  or or_8 (or_8_out, not_11_out, or_2_out);
  and and_10 (and_10_out, or_6_out, or_1_out);
  and and_11 (and_11_out, not_9_out, not_10_out);
  not not_12 (not_12_out, or_2_out);
  not not_13 (not_13_out, or_3_out);
  or or_9 (or_9_out, and_7_out, xnor_1_out, or_2_out);
  or or_10 (or_10_out, xnor_2_out, not_11_out);
  or or_11 (or_11_out, and_8_out, not_12_out);
  or or_12 (or_12_out, xnor_1_out, and_9_out);
  and and_12 (and_12_out, or_8_out, not_13_out);
  or or_13 (or_13_out, and_1_out, and_10_out, and_11_out);
  or or_14 (or_14_out, and_1_out, and_5_out, and_6_out);

  // Notes on the sheet:
  //   Design instructions:
  //   Click on the individual switches
  //   Default value is 0
  //   ENCODER
  //   The encoder, data bus, and decoder are labeled accordingly
  //   To enable the 7-segment display, the user must be in poke mode
  //   The 7-segment display output is located at the top-left corner of this script
  //   There are 7 switches located at the left side of the logism project script labeled from car_0 to car_6
  //   No two or more switches may equal 1 at the same time, because the output my be unexpected
  //   DATA BUS
  //   w
  //   x
  //   y
  //   z
  //   DECODER
  //   a
  //   b
  //   c
  //   d
  //   e
  //   f
  //   g
endmodule
