// Logisim project Lab3_prob2.circ as structural Verilog: 1 circuit, main circuit main
module main (
);

  wire and_1_out, and_2_out, and_3_out, and_4_out, and_5_out, button_1_out, clock_1_out, nor_1_out,
       nor_2_out, nor_3_out, nor_4_out, not_1_out, not_2_out;

  Button button_1 (.out(button_1_out));
  Clock clock_1 (.out(clock_1_out));
  not not_1 (not_1_out, button_1_out);
  and and_1 (and_1_out, button_1_out, clock_1_out);
  and and_2 (and_2_out, clock_1_out, not_1_out);
  nor nor_1 (nor_1_out, and_1_out, nor_2_out);
  nor nor_2 (nor_2_out, nor_1_out, and_2_out);
  not not_2 (not_2_out, clock_1_out);
  and and_3 (and_3_out, button_1_out, nor_4_out);
  and and_4 (and_4_out, nor_2_out, clock_1_out);
  and and_5 (and_5_out, not_2_out, and_3_out);
  nor nor_3 (nor_3_out, and_4_out, nor_4_out);
  nor nor_4 (nor_4_out, nor_3_out, and_5_out);
  LED led_1 (.in(nor_4_out));

  // Notes on the sheet:
  //   7433 x1
  //   7408 x2 
  //   7404 x1
  //   A1
  //   B2
  //   1A
  //   1Y
  //   Y1
  //   A2
  //   Y2
  //   B2
  //   1A
  //   1B
  //   2A
  //   2B
  //   Pin numbers beginning with numbers are associated to the 7433 chip
  //   Pin numbers beginning with letters are associated to the 7408 chip
  //   Circuit was tested under 1 hz of tick frequency
  //   1Y
  //   2A
  //   2Y
  //   A1
  //   Pin numbers for 7404 also begin with numbers, and they are the labels closest to the inverter gates
  //   A3
  //   B3
  //   A4
  //   2Y
  //   B4
  //   Y1
  //   B1
  //   Y3
  //   3A
  //   3B
  //   4A
  //   Y4
  //   4B
  //   3Y
  //   4Y
endmodule
