// Logisim project Lab3_prob3.circ as structural Verilog: 5 circuits, main circuit main
module main (
  input  I_O_Enable
);

  wire A1_out, A2_2_out, A2_out, A3_out, Clk_out, combinational_cicuit_1_out_6, combinational_cicuit_1_out_7,
       combinational_cicuit_1_out_8, combinational_cicuit_1_out_9, combinational_cicuit_1_out_10,
       combinational_cicuit_1_out_11, combinational_cicuit_1_out_12, combinational_cicuit_1_out_13,
       combinational_cicuit_1_out_14, combinational_cicuit_1_out_15, combinational_cicuit_1_out_16,
       combinational_cicuit_1_out_17, combinational_cicuit_1_out_18, combinational_cicuit_1_out_19,
       memory_1_out_3, memory_2_out_3, memory_3_out_3, memory_4_out_3, memory_5_out_3, memory_6_out_3,
       memory_7_out_3, register_1_out_6, register_1_out_7, register_1_out_8, register_1_out_9;

  Button A2 (.out(A2_out));
  Clock Clk (.out(Clk_out));
  Button A2_2 (.out(A2_2_out));
  Button A1 (.out(A1_out));
  Register register_1 (
    .A3(A3_out), .A2(A2_2_out), .A1(A1_out), .A0(A2_out), .Time(Clk_out), .out_6(register_1_out_6),
    .out_7(register_1_out_7), .out_8(register_1_out_8), .out_9(register_1_out_9));
  Combinational_Cicuit combinational_cicuit_1 (
    .in_3(I_O_Enable), .A0(register_1_out_9), .A1(register_1_out_8), .A2(register_1_out_7),
    .A3(register_1_out_6), .out_6(combinational_cicuit_1_out_6), .out_7(combinational_cicuit_1_out_7),
    .out_8(combinational_cicuit_1_out_8), .out_9(combinational_cicuit_1_out_9),
    .out_10(combinational_cicuit_1_out_10), .out_11(combinational_cicuit_1_out_11),
    .out_12(combinational_cicuit_1_out_12), .out_13(combinational_cicuit_1_out_13),
    .out_14(combinational_cicuit_1_out_14), .out_15(combinational_cicuit_1_out_15),
    .out_16(combinational_cicuit_1_out_16), .out_17(combinational_cicuit_1_out_17),
    .out_18(combinational_cicuit_1_out_18), .out_19(combinational_cicuit_1_out_19));
  Button A3 (.out(A3_out));
  LED A_C (.in(memory_1_out_3));
  Memory memory_1 (.in_1(combinational_cicuit_1_out_6), .in_2(combinational_cicuit_1_out_7), .out_3(memory_1_out_3));
  LED Door_1_Lock (.in(memory_2_out_3));
  Memory memory_2 (.in_1(combinational_cicuit_1_out_8), .in_2(combinational_cicuit_1_out_9), .out_3(memory_2_out_3));
  Memory memory_3 (.in_1(combinational_cicuit_1_out_10), .in_2(combinational_cicuit_1_out_11), .out_3(memory_3_out_3));
  LED Door_2_Lock (.in(memory_3_out_3));
  Memory memory_4 (.in_1(combinational_cicuit_1_out_12), .in_2(combinational_cicuit_1_out_13), .out_3(memory_4_out_3));
  LED Door_3_Lock (.in(memory_4_out_3));
  Memory memory_5 (.in_1(combinational_cicuit_1_out_14), .in_2(combinational_cicuit_1_out_15), .out_3(memory_5_out_3));
  LED Door_4_Lock (.in(memory_5_out_3));
  LED Engine_On (.in(memory_6_out_3));
  Memory memory_6 (.in_1(combinational_cicuit_1_out_16), .in_2(combinational_cicuit_1_out_17), .out_3(memory_6_out_3));
  LED Windshield_Wipers (.in(memory_7_out_3));
  Memory memory_7 (.in_1(combinational_cicuit_1_out_18), .in_2(combinational_cicuit_1_out_19), .out_3(memory_7_out_3));

  // Notes on the sheet:
  //   4 Bit Adress Bus
  //   I/O Control Circuit
  //   Actuators Control Lines
endmodule

module Memory (
  input  in_1,
  input  in_2,
  output out_3
);

  wire nor_1_out;

  nor nor_1 (nor_1_out, in_1, out_3);
  nor nor_2 (out_3, nor_1_out, in_2);
endmodule

// Combinational Circuit
module Combinational_Cicuit (
  input  A0,
  input  A2,
  input  in_3,
  input  A1,
  input  A3,
  output out_6,
  output out_7,
  output out_8,
  output out_9,
  output out_10,
  output out_11,
  output out_12,
  output out_13,
  output out_14,
  output out_15,
  output out_16,
  output out_17,
  output out_18,
  output out_19
);

  wire not_1_out, not_2_out, not_3_out, not_4_out, not_5_out, not_6_out, not_7_out, not_8_out, not_9_out,
       not_10_out, not_11_out, not_12_out, not_13_out, not_14_out, not_15_out, not_16_out, not_17_out,
       not_18_out, not_19_out, not_20_out, not_21_out, not_22_out, not_23_out, not_24_out, not_25_out,
       not_26_out, not_27_out, not_28_out, not_29_out, not_30_out, not_31_out;

  not not_1 (not_1_out, A3);
  not not_2 (not_2_out, A2);
  not not_3 (not_3_out, A1);
  not not_4 (not_4_out, A0);
  not not_5 (not_5_out, A3);
  not not_6 (not_6_out, A3);
  not not_7 (not_7_out, A2);
  not not_8 (not_8_out, A1);
  not not_9 (not_9_out, A2);
  not not_10 (not_10_out, A1);
  not not_11 (not_11_out, A0);
  not not_12 (not_12_out, A3);
  not not_13 (not_13_out, A2);
  not not_14 (not_14_out, A0);
  not not_15 (not_15_out, A2);
  not not_16 (not_16_out, A1);
  not not_17 (not_17_out, A3);
  not not_18 (not_18_out, A2);
  not not_19 (not_19_out, A2);
  not not_20 (not_20_out, A0);
  not not_21 (not_21_out, A3);
  not not_22 (not_22_out, A1);
  not not_23 (not_23_out, A0);
  not not_24 (not_24_out, A2);
  not not_25 (not_25_out, A3);
  not not_26 (not_26_out, A1);
  not not_27 (not_27_out, A1);
  not not_28 (not_28_out, A0);
  not not_29 (not_29_out, A3);
  not not_30 (not_30_out, A0);
  not not_31 (not_31_out, A1);
  and A_C_On (out_6, not_1_out, not_2_out, not_3_out, not_4_out, in_3);
  and A_C_Off (out_7, not_5_out, A2, A1, A0, in_3);
  and D1_L (out_8, not_6_out, not_7_out, not_8_out, A0, in_3);
  and D1_UL (out_9, A3, not_9_out, not_10_out, not_11_out, in_3);
  and D2_L (out_10, not_12_out, not_13_out, A1, not_14_out, in_3);
  and D2_UL (out_11, A3, not_15_out, not_16_out, A0, in_3);
  and D3_L (out_12, not_17_out, not_18_out, A1, A0, in_3);
  and D3_UL (out_13, A3, not_19_out, A1, not_20_out, in_3);
  and D4_L (out_14, not_21_out, A2, not_22_out, not_23_out, in_3);
  and D4_UL (out_15, A3, not_24_out, A1, A0, in_3);
  and Engine_On (out_16, not_25_out, A2, not_26_out, A0, in_3);
  and Engine_Off (out_17, A3, A2, not_27_out, not_28_out, in_3);
  and WW_On (out_18, not_29_out, A2, A1, not_30_out, in_3);
  and WW_Off (out_19, A3, A2, not_31_out, A0, in_3);
endmodule

module Register (
  input  A3,
  input  A2,
  input  A1,
  input  A0,
  input  Time,
  output out_6,
  output out_7,
  output out_8,
  output out_9
);

  wire and_1_out, and_2_out, and_3_out, and_4_out, and_5_out, and_6_out, and_7_out, and_8_out, and_9_out,
       and_10_out, and_11_out, and_12_out, and_13_out, and_14_out, and_15_out, and_16_out, and_17_out,
       and_18_out, and_19_out, and_20_out, nor_1_out, nor_2_out, nor_3_out, nor_4_out, nor_5_out, nor_6_out,
       nor_7_out, nor_8_out, nor_9_out, nor_11_out, nor_13_out, nor_15_out, not_1_out, not_2_out, not_3_out,
       not_4_out, not_5_out, not_6_out, not_7_out, not_8_out;

  and and_1 (and_1_out, A3, Time);
  and and_2 (and_2_out, Time, not_1_out);
  not not_1 (not_1_out, A3);
  and and_3 (and_3_out, A2, Time);
  and and_4 (and_4_out, Time, not_2_out);
  not not_2 (not_2_out, A2);
  and and_5 (and_5_out, A1, Time);
  and and_6 (and_6_out, Time, not_3_out);
  not not_3 (not_3_out, A1);
  and and_7 (and_7_out, A0, Time);
  and and_8 (and_8_out, Time, not_4_out);
  not not_4 (not_4_out, A0);
  nor nor_1 (nor_1_out, and_1_out, nor_2_out);
  nor nor_2 (nor_2_out, nor_1_out, and_2_out);
  nor nor_3 (nor_3_out, and_3_out, nor_4_out);
  nor nor_4 (nor_4_out, nor_3_out, and_4_out);
  nor nor_5 (nor_5_out, and_5_out, nor_6_out);
  nor nor_6 (nor_6_out, nor_5_out, and_6_out);
  nor nor_7 (nor_7_out, and_7_out, nor_8_out);
  nor nor_8 (nor_8_out, nor_7_out, and_8_out);
  not not_5 (not_5_out, Time);
  and and_9 (and_9_out, A3, out_6);
  not not_6 (not_6_out, Time);
  and and_10 (and_10_out, A2, out_7);
  not not_7 (not_7_out, Time);
  and and_11 (and_11_out, A1, out_8);
  not not_8 (not_8_out, Time);
  and and_12 (and_12_out, A0, out_9);
  and and_13 (and_13_out, nor_2_out, Time);
  and and_14 (and_14_out, not_5_out, and_9_out);
  and and_15 (and_15_out, nor_4_out, Time);
  and and_16 (and_16_out, not_6_out, and_10_out);
  and and_17 (and_17_out, nor_6_out, Time);
  and and_18 (and_18_out, not_7_out, and_11_out);
  and and_19 (and_19_out, nor_8_out, Time);
  and and_20 (and_20_out, not_8_out, and_12_out);
  nor nor_9 (nor_9_out, and_13_out, out_6);
  nor nor_10 (out_6, nor_9_out, and_14_out);
  nor nor_11 (nor_11_out, and_15_out, out_7);
  nor nor_12 (out_7, nor_11_out, and_16_out);
  nor nor_13 (nor_13_out, and_17_out, out_8);
  nor nor_14 (out_8, nor_13_out, and_18_out);
  nor nor_15 (nor_15_out, and_19_out, out_9);
  nor nor_16 (out_9, nor_15_out, and_20_out);

  // Notes on the sheet:
  //   Flip Flops
endmodule

module Time_Delay (
  input  in_1,
  input  in_2,
  input  in_3,
  input  in_4,
  input  Time,
  input  I_O_Enable,
  output out_7,
  output out_8,
  output out_9,
  output out_10
);

  wire and_1_out, and_2_out, and_3_out, and_4_out, and_5_out, and_6_out, and_7_out, and_8_out, and_9_out,
       and_10_out, and_11_out, and_12_out, and_13_out, and_14_out, and_15_out, and_16_out, and_17_out,
       nor_1_out, nor_2_out, nor_3_out, nor_4_out, nor_5_out, nor_6_out, nor_7_out, nor_8_out, nor_10_out,
       nor_12_out, nor_14_out, nor_16_out, not_1_out, not_2_out, not_3_out, not_4_out, not_5_out, not_6_out,
       not_7_out, not_8_out, not_9_out, not_10_out, not_11_out, not_12_out;

  and and_1 (and_1_out, Time, I_O_Enable);
  not not_1 (not_1_out, in_1);
  not not_2 (not_2_out, in_2);
  not not_3 (not_3_out, in_3);
  not not_4 (not_4_out, in_4);
  and and_2 (and_2_out, in_1, and_1_out);
  and and_3 (and_3_out, and_1_out, not_1_out);
  and and_4 (and_4_out, in_2, and_1_out);
  and and_5 (and_5_out, and_1_out, not_2_out);
  and and_6 (and_6_out, in_3, and_1_out);
  and and_7 (and_7_out, and_1_out, not_3_out);
  and and_8 (and_8_out, in_4, and_1_out);
  and and_9 (and_9_out, and_1_out, not_4_out);
  nor nor_1 (nor_1_out, and_2_out, nor_2_out);
  nor nor_2 (nor_2_out, nor_1_out, and_3_out);
  not not_5 (not_5_out, and_1_out);
  nor nor_3 (nor_3_out, and_4_out, nor_4_out);
  nor nor_4 (nor_4_out, nor_3_out, and_5_out);
  not not_6 (not_6_out, and_1_out);
  nor nor_5 (nor_5_out, and_6_out, nor_6_out);
  nor nor_6 (nor_6_out, nor_5_out, and_7_out);
  not not_7 (not_7_out, and_1_out);
  nor nor_7 (nor_7_out, and_8_out, nor_8_out);
  nor nor_8 (nor_8_out, nor_7_out, and_9_out);
  not not_8 (not_8_out, and_1_out);
  not not_9 (not_9_out, nor_2_out);
  not not_10 (not_10_out, nor_4_out);
  not not_11 (not_11_out, nor_6_out);
  not not_12 (not_12_out, nor_8_out);
  and and_10 (and_10_out, not_9_out, not_5_out);
  and and_11 (and_11_out, nor_2_out, not_5_out);
  and and_12 (and_12_out, not_10_out, not_6_out);
  and and_13 (and_13_out, nor_4_out, not_6_out);
  and and_14 (and_14_out, not_11_out, not_7_out);
  and and_15 (and_15_out, nor_6_out, not_7_out);
  and and_16 (and_16_out, not_12_out, not_8_out);
  and and_17 (and_17_out, nor_8_out, not_8_out);
  nor nor_9 (out_7, and_10_out, nor_10_out);
  nor nor_10 (nor_10_out, out_7, and_11_out);
  nor nor_11 (out_8, and_12_out, nor_12_out);
  nor nor_12 (nor_12_out, out_8, and_13_out);
  nor nor_13 (out_9, and_14_out, nor_14_out);
  nor nor_14 (nor_14_out, out_9, and_15_out);
  nor nor_15 (out_10, and_16_out, nor_16_out);
  nor nor_16 (nor_16_out, out_10, and_17_out);
endmodule
