// Logisim project adder.circ as structural Verilog: 3 circuits, main circuit main
module main (
  input  [7:0] b,
  input  [7:0] a,
  output overflow,
  output [7:0] out_4
);

  wire full_adder_1_carry_out, full_adder_2_carry_out, full_adder_3_carry_out, full_adder_4_carry_out,
       full_adder_5_carry_out, full_adder_6_carry_out, half_adder_1_carry_out;

  half_adder half_adder_1 (.a(a[0]), .b(b[0]), .carry_out(half_adder_1_carry_out), .sum(out_4[0]));
  full_adder full_adder_1 (
    .a(a[1]), .b(b[1]), .carry_in(half_adder_1_carry_out), .carry_out(full_adder_1_carry_out), .sum(out_4[1]));
  full_adder full_adder_2 (
    .a(a[2]), .b(b[2]), .carry_in(full_adder_1_carry_out), .carry_out(full_adder_2_carry_out), .sum(out_4[2]));
  full_adder full_adder_3 (
    .a(a[3]), .b(b[3]), .carry_in(full_adder_2_carry_out), .carry_out(full_adder_3_carry_out), .sum(out_4[3]));
  full_adder full_adder_4 (
    .a(a[4]), .b(b[4]), .carry_in(full_adder_3_carry_out), .carry_out(full_adder_4_carry_out), .sum(out_4[4]));
  full_adder full_adder_5 (
    .a(a[5]), .b(b[5]), .carry_in(full_adder_4_carry_out), .carry_out(full_adder_5_carry_out), .sum(out_4[5]));
  full_adder full_adder_6 (
    .a(a[6]), .b(b[6]), .carry_in(full_adder_5_carry_out), .carry_out(full_adder_6_carry_out), .sum(out_4[6]));
  full_adder full_adder_7 (.a(a[7]), .b(b[7]), .carry_in(full_adder_6_carry_out), .carry_out(overflow), .sum(out_4[7]));
endmodule

module full_adder (
  input  a,
  input  b,
  input  carry_in,
  output carry_out,
  output sum
);

  wire and_1_out, and_2_out, and_3_out;

  and and_1 (and_1_out, a, b);
  and and_2 (and_2_out, carry_in, b);
  and and_3 (and_3_out, a, carry_in);
  xor xor_1 (sum, carry_in, b, a);
  or or_1 (carry_out, and_1_out, and_2_out, and_3_out);
endmodule

module half_adder (
  input  a,
  input  b,
  output carry_out,
  output sum
);

  xor xor_1 (sum, a, b);
  and and_1 (carry_out, a, b);
endmodule
