// Logisim project barrel shifter.circ as structural Verilog: 4 circuits, main circuit main
module main (
  input  [7:0] in_1,
  input  in_2,
  input  [2:0] in_3,
  output [7:0] out_4
);

  wire [7:0] n1shifter_1_out_4, n2shifter_1_out_4;

  _1shifter u_1shifter_1 (.enable(in_3[0]), .left(in_2), .in_1(in_1), .out_4(n1shifter_1_out_4));
  _2shifter u_2shifter_1 (.enable(in_3[1]), .left(in_2), .in_1(n1shifter_1_out_4), .out_4(n2shifter_1_out_4));
  _4shifter u_4shifter_1 (.enable(in_3[2]), .left(in_2), .in_1(n2shifter_1_out_4), .out_4(out_4));
endmodule

module _1shifter (
  input  [7:0] in_1,
  input  enable,
  input  left,
  output [7:0] out_4
);

  Multiplexer #(.select(2), .enable("false")) multiplexer_1 (
    .in0(in_1[7]), .in1(1'b0), .in2(in_1[7]), .in3(in_1[6]), .out(out_4[7]), .sel({left, enable}));
  Multiplexer #(.select(2), .enable("false")) multiplexer_2 (
    .in0(in_1[6]), .in1(in_1[7]), .in2(in_1[6]), .in3(in_1[5]), .out(out_4[6]), .sel({left, enable}));
  Multiplexer #(.select(2), .enable("false")) multiplexer_3 (
    .in0(in_1[5]), .in1(in_1[6]), .in2(in_1[5]), .in3(in_1[4]), .out(out_4[5]), .sel({left, enable}));
  Multiplexer #(.select(2), .enable("false")) multiplexer_4 (
    .in0(in_1[4]), .in1(in_1[5]), .in2(in_1[4]), .in3(in_1[3]), .out(out_4[4]), .sel({left, enable}));
  Multiplexer #(.select(2), .enable("false")) multiplexer_5 (
    .in0(in_1[3]), .in1(in_1[4]), .in2(in_1[3]), .in3(in_1[2]), .out(out_4[3]), .sel({left, enable}));
  Multiplexer #(.select(2), .enable("false")) multiplexer_6 (
    .in0(in_1[2]), .in1(in_1[3]), .in2(in_1[2]), .in3(in_1[1]), .out(out_4[2]), .sel({left, enable}));
  Multiplexer #(.select(2), .enable("false")) multiplexer_7 (
    .in0(in_1[1]), .in1(in_1[2]), .in2(in_1[1]), .in3(in_1[0]), .out(out_4[1]), .sel({left, enable}));
  Multiplexer #(.select(2), .enable("false")) multiplexer_8 (
    .in0(in_1[0]), .in1(in_1[1]), .in2(in_1[0]), .in3(1'b0), .out(out_4[0]), .sel({left, enable}));
endmodule

module _2shifter (
  input  [7:0] in_1,
  input  enable,
  input  left,
  output [7:0] out_4
);

  Multiplexer #(.select(2), .enable("false")) multiplexer_1 (
    .in0(in_1[7]), .in1(1'b0), .in2(in_1[7]), .in3(in_1[5]), .out(out_4[7]), .sel({left, enable}));
  Multiplexer #(.select(2), .enable("false")) multiplexer_2 (
    .in0(in_1[6]), .in1(1'b0), .in2(in_1[6]), .in3(in_1[4]), .out(out_4[6]), .sel({left, enable}));
  Multiplexer #(.select(2), .enable("false")) multiplexer_3 (
    .in0(in_1[5]), .in1(in_1[7]), .in2(in_1[5]), .in3(in_1[3]), .out(out_4[5]), .sel({left, enable}));
  Multiplexer #(.select(2), .enable("false")) multiplexer_4 (
    .in0(in_1[4]), .in1(in_1[6]), .in2(in_1[4]), .in3(in_1[2]), .out(out_4[4]), .sel({left, enable}));
  Multiplexer #(.select(2), .enable("false")) multiplexer_5 (
    .in0(in_1[3]), .in1(in_1[5]), .in2(in_1[3]), .in3(in_1[1]), .out(out_4[3]), .sel({left, enable}));
  Multiplexer #(.select(2), .enable("false")) multiplexer_6 (
    .in0(in_1[2]), .in1(in_1[4]), .in2(in_1[2]), .in3(in_1[0]), .out(out_4[2]), .sel({left, enable}));
  Multiplexer #(.select(2), .enable("false")) multiplexer_7 (
    .in0(in_1[1]), .in1(in_1[3]), .in2(in_1[1]), .in3(1'b0), .out(out_4[1]), .sel({left, enable}));
  Multiplexer #(.select(2), .enable("false")) multiplexer_8 (
    .in0(in_1[0]), .in1(in_1[2]), .in2(in_1[0]), .in3(1'b0), .out(out_4[0]), .sel({left, enable}));
endmodule

module _4shifter (
  input  [7:0] in_1,
  input  enable,
  input  left,
  output [7:0] out_4
);

  Multiplexer #(.select(2), .enable("false")) multiplexer_1 (
    .in0(in_1[7]), .in1(1'b0), .in2(in_1[7]), .in3(in_1[3]), .out(out_4[7]), .sel({left, enable}));
  Multiplexer #(.select(2), .enable("false")) multiplexer_2 (
    .in0(in_1[6]), .in1(1'b0), .in2(in_1[6]), .in3(in_1[2]), .out(out_4[6]), .sel({left, enable}));
  Multiplexer #(.select(2), .enable("false")) multiplexer_3 (
    .in0(in_1[5]), .in1(1'b0), .in2(in_1[5]), .in3(in_1[1]), .out(out_4[5]), .sel({left, enable}));
  Multiplexer #(.select(2), .enable("false")) multiplexer_4 (
    .in0(in_1[4]), .in1(1'b0), .in2(in_1[4]), .in3(in_1[0]), .out(out_4[4]), .sel({left, enable}));
  Multiplexer #(.select(2), .enable("false")) multiplexer_5 (
    .in0(in_1[3]), .in1(in_1[7]), .in2(in_1[3]), .in3(1'b0), .out(out_4[3]), .sel({left, enable}));
  Multiplexer #(.select(2), .enable("false")) multiplexer_6 (
    .in0(in_1[2]), .in1(in_1[6]), .in2(in_1[2]), .in3(1'b0), .out(out_4[2]), .sel({left, enable}));
  Multiplexer #(.select(2), .enable("false")) multiplexer_7 (
    .in0(in_1[1]), .in1(in_1[5]), .in2(in_1[1]), .in3(1'b0), .out(out_4[1]), .sel({left, enable}));
  Multiplexer #(.select(2), .enable("false")) multiplexer_8 (
    .in0(in_1[0]), .in1(in_1[4]), .in2(in_1[0]), .in3(1'b0), .out(out_4[0]), .sel({left, enable}));
endmodule
