// Logisim project comparator.circ as structural Verilog: 2 circuits, main circuit main
module main (
  input  [7:0] a,
  input  [7:0] b
);

  wire bit_compare_1_oeq, bit_compare_1_ogr, bit_compare_1_ols, bit_compare_2_oeq, bit_compare_2_ogr,
       bit_compare_2_ols, bit_compare_3_oeq, bit_compare_3_ogr, bit_compare_3_ols, bit_compare_4_oeq,
       bit_compare_4_ogr, bit_compare_4_ols, bit_compare_5_oeq, bit_compare_5_ogr, bit_compare_5_ols,
       bit_compare_6_oeq, bit_compare_6_ogr, bit_compare_6_ols, bit_compare_7_oeq, bit_compare_7_ogr,
       bit_compare_7_ols;

  bit_compare bit_compare_1 (
    .a(a[6]), .b(b[6]), .ils(bit_compare_2_ols), .ieq(bit_compare_2_oeq), .igr(bit_compare_2_ogr),
    .ols(bit_compare_1_ols), .oeq(bit_compare_1_oeq), .ogr(bit_compare_1_ogr));
  bit_compare bit_compare_2 (
    .a(a[7]), .b(b[7]), .ils(1'b0), .ieq(1'b1), .igr(1'b0), .ols(bit_compare_2_ols), .oeq(bit_compare_2_oeq),
    .ogr(bit_compare_2_ogr));
  bit_compare bit_compare_3 (
    .a(a[5]), .b(b[5]), .ils(bit_compare_1_ols), .ieq(bit_compare_1_oeq), .igr(bit_compare_1_ogr),
    .ols(bit_compare_3_ols), .oeq(bit_compare_3_oeq), .ogr(bit_compare_3_ogr));
  bit_compare bit_compare_4 (
    .a(a[4]), .b(b[4]), .ils(bit_compare_3_ols), .ieq(bit_compare_3_oeq), .igr(bit_compare_3_ogr),
    .ols(bit_compare_4_ols), .oeq(bit_compare_4_oeq), .ogr(bit_compare_4_ogr));
  bit_compare bit_compare_5 (
    .a(a[3]), .b(b[3]), .ils(bit_compare_4_ols), .ieq(bit_compare_4_oeq), .igr(bit_compare_4_ogr),
    .ols(bit_compare_5_ols), .oeq(bit_compare_5_oeq), .ogr(bit_compare_5_ogr));
  bit_compare bit_compare_6 (
    .a(a[2]), .b(b[2]), .ils(bit_compare_5_ols), .ieq(bit_compare_5_oeq), .igr(bit_compare_5_ogr),
    .ols(bit_compare_6_ols), .oeq(bit_compare_6_oeq), .ogr(bit_compare_6_ogr));
  bit_compare bit_compare_7 (
    .a(a[1]), .b(b[1]), .ils(bit_compare_6_ols), .ieq(bit_compare_6_oeq), .igr(bit_compare_6_ogr),
    .ols(bit_compare_7_ols), .oeq(bit_compare_7_oeq), .ogr(bit_compare_7_ogr));
  bit_compare bit_compare_8 (
    .a(a[0]), .b(b[0]), .ils(bit_compare_7_ols), .ieq(bit_compare_7_oeq), .igr(bit_compare_7_ogr));  // open: ols, oeq, ogr
endmodule

module bit_compare (
  input  a,
  input  b,
  input  ils,
  input  ieq,
  input  igr,
  output ols,
  output oeq,
  output ogr
);

  wire and_1_out, and_2_out, and_3_out, and_4_out, not_1_out, not_2_out, not_3_out, not_4_out, or_2_out;

  not not_1 (not_1_out, a);
  not not_2 (not_2_out, a);
  not not_3 (not_3_out, b);
  not not_4 (not_4_out, b);
  and and_1 (and_1_out, ieq, not_1_out, b);
  and and_2 (and_2_out, a, b);
  and and_3 (and_3_out, not_2_out, not_3_out);
  and and_4 (and_4_out, ieq, a, not_4_out);
  or or_1 (ols, ils, and_1_out);
  and and_5 (oeq, ieq, or_2_out);
  or or_2 (or_2_out, and_2_out, and_3_out);
  or or_3 (ogr, igr, and_4_out);
endmodule
