// Logisim project counter.circ as structural Verilog: 7 circuits, main circuit main
module main (
  input  clock,
  input  Left,
  input  Right,
  output out_4,
  output out_5,
  output out_6,
  output out_7,
  output out_8
);

  wire and_1_out, and_2_out, not_1_out, or_1_out, terminal_1_out_2, terminal_b_1_out_2;
  wire [4:0] decrementer_b_1_out_2, incrementor_1_out_2, multiplexer_1_out, register_1_q, register_2_q;

  or or_1 (or_1_out, ~Left, terminal_1_out_2);  // OR_Gate
  Register #(.width(5)) register_1 (
    .D(incrementor_1_out_2), .Q(register_1_q), .clk(and_1_out), .clr(or_1_out));  // open: en
  and and_1 (and_1_out, clock, Left);
  incrementor incrementor_1 (.in_1(register_1_q), .out_2(incrementor_1_out_2));
  terminal terminal_1 (.in_1(register_1_q), .out_2(terminal_1_out_2));
  xor xor_1 (out_4, register_1_q[4], register_2_q[4]);
  and and_2 (and_2_out, clock, Right);
  xor xor_2 (out_5, register_1_q[3], register_2_q[3]);
  xor xor_3 (out_6, register_1_q[2], register_2_q[2]);
  Multiplexer #(.width(5), .enable("false")) multiplexer_1 (
    .in0(decrementer_b_1_out_2), .in1(5'b10100), .out(multiplexer_1_out), .sel(terminal_b_1_out_2));
  Register #(.width(5)) register_2 (
    .D(multiplexer_1_out), .Q(register_2_q), .clk(and_2_out), .clr(not_1_out));  // open: en
  not not_1 (not_1_out, Right);
  xor xor_4 (out_7, register_1_q[1], register_2_q[1]);
  decrementer_b decrementer_b_1 (.in_1(register_2_q), .out_2(decrementer_b_1_out_2));
  terminal_b terminal_b_1 (.in_1(register_2_q), .out_2(terminal_b_1_out_2));
  xor xor_5 (out_8, register_1_q[0], register_2_q[0]);
endmodule

module incrementor (
  input  [4:0] in_1,
  output [4:0] out_2
);

  wire half_adder_1_carry_out, half_adder_3_carry_out, half_adder_4_carry_out, half_adder_5_carry_out;

  half_adder half_adder_1 (.a(half_adder_3_carry_out), .b(in_1[3]), .carry_out(half_adder_1_carry_out), .sum(out_2[3]));
  half_adder half_adder_2 (.a(half_adder_1_carry_out), .b(in_1[4]), .sum(out_2[4]));  // open: carry_out
  half_adder half_adder_3 (.a(half_adder_4_carry_out), .b(in_1[2]), .carry_out(half_adder_3_carry_out), .sum(out_2[2]));
  half_adder half_adder_4 (.a(half_adder_5_carry_out), .b(in_1[1]), .carry_out(half_adder_4_carry_out), .sum(out_2[1]));
  half_adder half_adder_5 (.a(1'b1), .b(in_1[0]), .carry_out(half_adder_5_carry_out), .sum(out_2[0]));
endmodule

module terminal (
  input  [4:0] in_1,
  output out_2
);

  Comparator #(.width(5)) comparator_1 (.a(5'b10101), .b(in_1), .eq(out_2));  // open: gt, lt
endmodule

module decrementer (
  input  [4:0] in_1,
  output [4:0] out_2
);

  wire half_adder_2_carry_out, half_adder_3_carry_out, half_adder_4_carry_out, half_adder_5_carry_out;

  half_adder half_adder_1 (.a(half_adder_2_carry_out), .b(in_1[4]), .sum(out_2[4]));  // open: carry_out
  half_adder half_adder_2 (.a(half_adder_3_carry_out), .b(in_1[3]), .carry_out(half_adder_2_carry_out), .sum(out_2[3]));
  half_adder half_adder_3 (.a(half_adder_4_carry_out), .b(in_1[2]), .carry_out(half_adder_3_carry_out), .sum(out_2[2]));
  half_adder half_adder_4 (.a(half_adder_5_carry_out), .b(in_1[1]), .carry_out(half_adder_4_carry_out), .sum(out_2[1]));
  half_adder half_adder_5 (.a(1'b1), .b(in_1[0]), .carry_out(half_adder_5_carry_out), .sum(out_2[0]));
endmodule

// ter_b
module terminal_b (
  input  [4:0] in_1,
  output out_2
);

  Comparator #(.width(5), .mode("unsigned")) comparator_1 (.a({5{1'b0}}), .b(in_1), .eq(out_2));  // open: gt, lt
endmodule

module complement (
  input  [4:0] in_1,
  output [4:0] out_2
);

  wire [4:0] not_1_out;

  assign not_1_out = ~in_1;  // NOT_Gate not_1, 5 bits wide
  decrementer decrementer_1 (.in_1(not_1_out), .out_2(out_2));
endmodule

// dec_b
module decrementer_b (
  input  [4:0] in_1,
  output [4:0] out_2
);

  Subtractor #(.width(5)) subtractor_1 (.a(in_1), .b(5'b00001), .out(out_2));  // open: bin, bout
endmodule
