// Logisim project lab4_prob1.circ as structural Verilog: 2 circuits, main circuit main
module main (
);

  wire clock_2_out, clock_out, decoder_1_out_6, decoder_1_out_7, decoder_1_out_8, decoder_1_out_9,
       decoder_1_out_10, decoder_1_out_11, decoder_1_out_12, decoder_1_out_13, decoder_1_out_14,
       decoder_1_out_15, decoder_1_out_16, decoder_1_out_17, decoder_1_out_18, decoder_1_out_19,
       decoder_1_out_20, decoder_1_out_21, decoder_1_out_22, decoder_1_out_23, decoder_1_out_24,
       decoder_1_out_25, Left_Signal_2_out, Left_Signal_out, main_2_out_4, main_2_out_5, main_2_out_6,
       main_2_out_7, main_2_out_8, Right_Signal_2_out, Right_Signal_out;
  wire [4:0] main_1_out_8;
  wire [19:0] rom_1_data;

  Clock clock (.out(clock_out));
  Button Left_Signal (.out(Left_Signal_out));
  Button Right_Signal (.out(Right_Signal_out));
  LED led_1 (.in(decoder_1_out_7));
  LED led_2 (.in(decoder_1_out_6));
  LED led_3 (.in(decoder_1_out_9));
  LED led_4 (.in(decoder_1_out_8));
  counter_main main_1 (
    .clock(clock_out), .Left(Left_Signal_out), .Right(Right_Signal_out), .out_4(main_1_out_8[4]),
    .out_5(main_1_out_8[3]), .out_6(main_1_out_8[2]), .out_7(main_1_out_8[1]), .out_8(main_1_out_8[0]));
  LED led_5 (.in(rom_1_data[19]));
  LED led_6 (.in(rom_1_data[17]));
  LED led_7 (.in(rom_1_data[18]));
  LED led_8 (.in(decoder_1_out_13));
  LED led_9 (.in(decoder_1_out_12));
  LED led_10 (.in(decoder_1_out_10));
  LED led_11 (.in(decoder_1_out_11));
  LED led_12 (.in(rom_1_data[14]));
  LED led_13 (.in(rom_1_data[15]));
  LED led_14 (.in(rom_1_data[16]));
  Clock clock_2 (.out(clock_2_out));
  Button Left_Signal_2 (.out(Left_Signal_2_out));
  Button Right_Signal_2 (.out(Right_Signal_2_out));
  LED led_15 (.in(decoder_1_out_15));
  LED led_16 (.in(decoder_1_out_14));
  LED led_17 (.in(rom_1_data[12]));
  LED led_18 (.in(rom_1_data[13]));
  counter_main main_2 (
    .clock(clock_2_out), .Left(Left_Signal_2_out), .Right(Right_Signal_2_out), .out_4(main_2_out_4),
    .out_5(main_2_out_5), .out_6(main_2_out_6), .out_7(main_2_out_7), .out_8(main_2_out_8));
  decoder decoder_1 (
    .in_3(main_2_out_4), .in_1(main_2_out_5), .in_4(main_2_out_6), .in_2(main_2_out_7), .in_5(main_2_out_8),
    .out_6(decoder_1_out_6), .out_7(decoder_1_out_7), .out_8(decoder_1_out_8), .out_9(decoder_1_out_9),
    .out_10(decoder_1_out_10), .out_11(decoder_1_out_11), .out_12(decoder_1_out_12),
    .out_13(decoder_1_out_13), .out_14(decoder_1_out_14), .out_15(decoder_1_out_15),
    .out_16(decoder_1_out_16), .out_17(decoder_1_out_17), .out_18(decoder_1_out_18),
    .out_19(decoder_1_out_19), .out_20(decoder_1_out_20), .out_21(decoder_1_out_21),
    .out_22(decoder_1_out_22), .out_23(decoder_1_out_23), .out_24(decoder_1_out_24), .out_25(decoder_1_out_25));
  LED led_19 (.in(rom_1_data[10]));
  LED led_20 (.in(rom_1_data[11]));
  LED led_21 (.in(rom_1_data[9]));
  ROM #(.addrWidth(5), .dataWidth(20)) rom_1 (.addr(main_1_out_8), .data(rom_1_data));  // open: sel
  LED led_22 (.in(rom_1_data[7]));
  LED led_23 (.in(rom_1_data[8]));
  LED led_24 (.in(rom_1_data[6]));
  LED led_25 (.in(decoder_1_out_16));
  LED led_26 (.in(decoder_1_out_17));
  LED led_27 (.in(decoder_1_out_18));
  LED led_28 (.in(rom_1_data[5]));
  LED led_29 (.in(rom_1_data[4]));
  LED led_30 (.in(decoder_1_out_21));
  LED led_31 (.in(decoder_1_out_22));
  LED led_32 (.in(decoder_1_out_19));
  LED led_33 (.in(decoder_1_out_20));
  LED led_34 (.in(rom_1_data[1]));
  LED led_35 (.in(rom_1_data[2]));
  LED led_36 (.in(rom_1_data[3]));
  LED led_37 (.in(decoder_1_out_24));
  LED led_38 (.in(decoder_1_out_25));
  LED led_39 (.in(decoder_1_out_23));
  LED led_40 (.in(rom_1_data[0]));

  // Notes on the sheet:
  //   contents of rom_1 (hex, n*v repeats v):
  //   0 1 2 4 8 10 20 40 80 100 200 400 800 1000 2000 4000 8000 10000 20000 40000 80000
endmodule

module decoder (
  input  in_1,
  input  in_2,
  input  in_3,
  input  in_4,
  input  in_5,
  output out_6,
  output out_7,
  output out_8,
  output out_9,
  output out_10,
  output out_11,
  output out_12,
  output out_13,
  output out_14,
  output out_15,
  output out_16,
  output out_17,
  output out_18,
  output out_19,
  output out_20,
  output out_21,
  output out_22,
  output out_23,
  output out_24,
  output out_25
);

  wire not_1_out, not_2_out, not_3_out, not_4_out, not_5_out, not_6_out, not_7_out, not_8_out;

  and and_1 (out_6, in_3, ~in_1, in_4, ~in_2, ~in_5);  // AND_Gate
  and and_2 (out_7, in_3, ~in_1, ~in_4, in_2, in_5);  // AND_Gate
  and and_3 (out_8, in_3, ~in_1, ~in_4, in_2, ~in_5);  // AND_Gate
  and and_4 (out_9, in_3, ~in_1, ~in_4, ~in_2, in_5);  // AND_Gate
  and and_5 (out_10, in_3, ~in_1, ~in_4, ~in_2, ~in_5);  // AND_Gate
  and and_6 (out_11, ~in_3, in_1, in_4, in_2, in_5);  // AND_Gate
  and and_7 (out_12, ~in_3, in_1, in_4, in_2, ~in_5);  // AND_Gate
  and and_8 (out_13, ~in_3, in_1, in_4, ~in_2, in_5);  // AND_Gate
  and and_9 (out_14, ~in_3, in_1, in_4, ~in_2, ~in_5);  // AND_Gate
  and and_10 (out_15, ~in_3, in_1, ~in_4, in_2, in_5);  // AND_Gate
  and and_11 (out_17, ~in_3, in_1, ~in_4, ~in_2, in_5);  // AND_Gate
  and and_12 (out_16, ~in_3, in_1, ~in_4, in_2, ~in_5);  // AND_Gate
  and and_13 (out_18, ~in_3, in_1, ~in_4, ~in_2, ~in_5);  // AND_Gate
  and and_14 (out_19, ~in_3, ~in_1, in_4, in_2, in_5);  // AND_Gate
  and and_15 (out_20, ~in_3, ~in_1, in_4, in_2, ~in_5);  // AND_Gate
  and and_16 (out_21, ~in_3, ~in_1, in_4, ~in_2, in_5);  // AND_Gate
  and and_17 (out_22, ~in_3, ~in_1, in_4, ~in_2, ~in_5);  // AND_Gate
  not not_1 (not_1_out, in_3);
  and and_18 (out_23, ~in_3, ~in_1, ~in_4, in_2, in_5);  // AND_Gate
  not not_2 (not_2_out, in_1);
  not not_3 (not_3_out, in_3);
  not not_4 (not_4_out, in_5);
  not not_5 (not_5_out, in_1);
  not not_6 (not_6_out, in_4);
  not not_7 (not_7_out, in_4);
  and and_19 (out_25, not_3_out, not_2_out, not_6_out, not_8_out, in_5);
  and and_20 (out_24, not_1_out, not_5_out, not_7_out, in_2, not_4_out);
  not not_8 (not_8_out, in_2);
endmodule
