// Logisim project lab4_prob2.circ as structural Verilog: 4 circuits, main circuit main
module main (
  input  [7:0] Input_device,
  input  [7:0] Unidirectional_add,
  input  [7:0] Bidirectional_in,
  input  [5:0] In_control_line,
  output [7:0] Output_device,
  output [7:0] bidirectional_bus,
  output [7:0] out_7,
  output [7:0] out_8,
  output [7:0] out_9
);

  wire clock_1_out;
  wire [7:0] controlled_buffer_1_out, controlled_buffer_2_out, rom_1_data;

  assign controlled_buffer_1_out = In_control_line[0] ? Unidirectional_add : 8'bz;  // Controlled_Buffer controlled_buffer_1
  ROM rom_1 (.addr(controlled_buffer_1_out), .data(rom_1_data), .sel(In_control_line[1]));
  assign controlled_buffer_2_out = In_control_line[2] ? Unidirectional_add : 8'bz;  // Controlled_Buffer controlled_buffer_2
  Register register_1 (.D(rom_1_data), .Q(out_7), .clk(clock_1_out));  // open: en, clr
  Clock clock_1 (.out(clock_1_out));
  RAM #(.bus("separate")) ram_1 (
    .addr(controlled_buffer_2_out), .din(out_7), .data(out_8), .str(In_control_line[4]),
    .sel(In_control_line[3]), .clk(clock_1_out), .ld(In_control_line[4]), .clr(In_control_line[5]));
  I_O_System i_o_system_1 (
    .in_2(Unidirectional_add), .in_3(Bidirectional_in), .in_1(Input_device), .out_6(out_9),
    .out_4(Output_device), .out_5(bidirectional_bus));

  // Notes on the sheet:
  //   These three outputs go in the cpu
  //   contents of rom_1 (hex, n*v repeats v):
  //   9 87 56 45 251*0 ff
endmodule

// I/O Subsystem
module I_O_System (
  input  [7:0] in_1,
  input  [7:0] in_2,
  input  [7:0] in_3,
  output [7:0] out_4,
  output [7:0] out_5,
  output [7:0] out_6
);

  _8_bit_Latch u_8_bit_latch_1 (
    .in_1(in_1), .out_2(out_6[0]), .out_3(out_6[1]), .out_4(out_6[2]), .out_5(out_6[3]), .out_6(out_6[4]),
    .out_7(out_6[5]), .out_8(out_6[6]), .out_9(out_6[7]));

  assign out_4 = in_2;
  assign out_5 = in_3;

  // Notes on the sheet:
  //   Takes in input from bidirectional bus
  //   Input from the adress bus goes to an output device
  //   Input from the input device
  //   Output from the input device goes to bidirectional data bus
  //   This represents the output device
  //   This represents the second bidirectional bus
  //   (Shown on the diagram)
endmodule

// 8-bit latch
module _8_bit_Latch (
  input  [7:0] in_1,
  output out_2,
  output out_3,
  output out_4,
  output out_5,
  output out_6,
  output out_7,
  output out_8,
  output out_9
);

  wire clock_1_out;

  Clock clock_1 (.out(clock_1_out));
  D_Flip_Flop d_ff_1 (.clk(clock_1_out), .D(in_1[0]), .Q(out_2));  // open: Qn, preset, en, reset
  D_Flip_Flop d_ff_2 (.clk(clock_1_out), .D(in_1[1]), .Q(out_3));  // open: Qn, preset, en, reset
  D_Flip_Flop d_ff_3 (.clk(clock_1_out), .D(in_1[2]), .Q(out_4));  // open: Qn, preset, en, reset
  D_Flip_Flop d_ff_4 (.clk(clock_1_out), .D(in_1[3]), .Q(out_5));  // open: Qn, preset, en, reset
  D_Flip_Flop d_ff_5 (.clk(clock_1_out), .D(in_1[4]), .Q(out_6));  // open: Qn, preset, en, reset
  D_Flip_Flop d_ff_6 (.clk(clock_1_out), .D(in_1[5]), .Q(out_7));  // open: Qn, preset, en, reset
  D_Flip_Flop d_ff_7 (.clk(clock_1_out), .D(in_1[6]), .Q(out_8));  // open: Qn, preset, en, reset
  D_Flip_Flop d_ff_8 (.clk(clock_1_out), .D(in_1[7]), .Q(out_9));  // open: Qn, preset, en, reset
endmodule

// 3x8_dec
module decoder (
  input  a,
  input  b,
  input  c,
  input  d,
  input  e,
  input  f,
  input  g,
  input  h,
  output x
);

  wire and_1_out, and_2_out, not_1_out, not_2_out, not_3_out, not_4_out, not_5_out, not_6_out;

  not not_1 (not_1_out, a);
  not not_2 (not_2_out, b);
  not not_3 (not_3_out, c);
  not not_4 (not_4_out, d);
  not not_5 (not_5_out, f);
  not not_6 (not_6_out, h);
  and and_1 (and_1_out, not_1_out, not_2_out, not_3_out, not_4_out, e, not_5_out, g, not_6_out);
  and and_2 (and_2_out, a, b, c, d, e, f, g, h);
  or or_1 (x, and_1_out, and_2_out);
endmodule
