// Logisim project subtractor.circ as structural Verilog: 4 circuits, main circuit main
module main (
  input  [7:0] b,
  input  [7:0] a,
  output [7:0] out_3
);

  wire full_adder_1_carry_out, full_adder_2_carry_out, full_adder_3_carry_out, full_adder_4_carry_out,
       full_adder_5_carry_out, full_adder_6_carry_out, half_adder_1_carry_out;
  wire [7:0] complement_1_out_2;

  complement complement_1 (.in_1(b), .out_2(complement_1_out_2));
  half_adder half_adder_1 (.a(a[0]), .b(complement_1_out_2[0]), .carry_out(half_adder_1_carry_out), .sum(out_3[0]));
  full_adder full_adder_1 (
    .a(a[1]), .b(complement_1_out_2[1]), .carry_in(half_adder_1_carry_out),
    .carry_out(full_adder_1_carry_out), .sum(out_3[1]));
  full_adder full_adder_2 (
    .a(a[3]), .b(complement_1_out_2[3]), .carry_in(full_adder_3_carry_out),
    .carry_out(full_adder_2_carry_out), .sum(out_3[3]));
  full_adder full_adder_3 (
    .a(a[2]), .b(complement_1_out_2[2]), .carry_in(full_adder_1_carry_out),
    .carry_out(full_adder_3_carry_out), .sum(out_3[2]));
  full_adder full_adder_4 (
    .a(a[4]), .b(complement_1_out_2[4]), .carry_in(full_adder_2_carry_out),
    .carry_out(full_adder_4_carry_out), .sum(out_3[4]));
  full_adder full_adder_5 (
    .a(a[5]), .b(complement_1_out_2[5]), .carry_in(full_adder_4_carry_out),
    .carry_out(full_adder_5_carry_out), .sum(out_3[5]));
  full_adder full_adder_6 (
    .a(a[6]), .b(complement_1_out_2[6]), .carry_in(full_adder_5_carry_out),
    .carry_out(full_adder_6_carry_out), .sum(out_3[6]));
  full_adder full_adder_7 (
    .a(a[7]), .b(complement_1_out_2[7]), .carry_in(full_adder_6_carry_out), .sum(out_3[7]));  // open: carry_out
endmodule

module full_adder (
  input  a,
  input  b,
  input  carry_in,
  output carry_out,
  output sum
);

  wire and_1_out, and_2_out, and_3_out;

  and and_1 (and_1_out, a, b);
  and and_2 (and_2_out, carry_in, b);
  and and_3 (and_3_out, a, carry_in);
  xor xor_1 (sum, carry_in, b, a);
  or or_1 (carry_out, and_1_out, and_2_out, and_3_out);
endmodule

module half_adder (
  input  a,
  input  b,
  output carry_out,
  output sum
);

  xor xor_1 (sum, a, b);
  and and_1 (carry_out, a, b);
endmodule

module complement (
  input  [7:0] in_1,
  output [7:0] out_2
);

  wire [7:0] not_1_out;

  assign not_1_out = ~in_1;  // NOT_Gate not_1, 8 bits wide
  // adder_main main_1: pin names not known; wires that end beside it: not_1_out, 8'h1, out_2
endmodule
